// Logisim project cache.circ as structural Verilog: 2 circuits, main circuit cache-entry
module main (
  input  [7:0] address,
  input  read_enable,
  input  [31:0] ROM_data_in,
  output [7:0] data_out,
  output [5:0] ROM_read_address,
  output ROM_read_enable
);

  Multiplexer #(.select(2), .width(8), .enable("false")) multiplexer_1 (
    .in0(ROM_data_in[7:0]), .in1(ROM_data_in[15:8]), .in2(ROM_data_in[23:16]), .in3(ROM_data_in[31:24]),
    .out(data_out), .sel(address[1:0]));

  assign ROM_read_address = address[7:2];
  assign ROM_read_enable = read_enable;

  // Notes on the sheet:
  //   data_out: pull=down
  //   ROM_read_address: pull=down
  //   ROM_read_enable: pull=down
endmodule

module cache_entry (
  input  [31:0] data_in,
  input  [3:0] tag,
  input  clock,
  output [31:0] data_out,
  output miss
);

  wire and_1_out, comparator_1_eq, valid_q;
  wire [3:0] tagreg_q;

  Register #(.width(32)) cache (.D(data_in), .en(miss), .Q(data_out), .clk(clock));  // open: clr
  Register #(.width(4)) tagreg (.D(tag), .en(miss), .Q(tagreg_q), .clk(clock));  // open: clr
  Register #(.width(1)) valid (.D(1'b1), .en(miss), .Q(valid_q), .clk(clock));  // open: clr
  Comparator #(.width(4)) comparator_1 (.a(tagreg_q), .b(tag), .eq(comparator_1_eq));  // open: gt, lt
  and and_1 (and_1_out, comparator_1_eq, valid_q);
  not not_1 (miss, and_1_out);
endmodule
